# Fritzing sketch az-delivery-waveshare-7c (saved by Fritzing 1.0.4)
breadboards: 1

parts:
  U1 = ESP32S-HiLetgo [part_number=ESP32S-HiLetgo]
  Part2 = BME280
  R1 = Resistor [tolerance=±5% resistance=100k package="2512 [SMD]"]
  R2 = Resistor [tolerance=±5% resistance=100k package="2512 [SMD]"]
  U2 = LIPO-2000mAh [package=lipo-2000]
  A1 = waveshare-e-Paper-HAT-with-7in-display_1
  S1 = Round Pushbutton

nets:
  N1: U1.3.3, A1.connector7
  N2: U1.EN, S1.leg1
  N3: U1.GPIO34, R1.Pin_0, R2.Pin_1
  N4: U1.GPIO25, Part2.SCL
  N5: U1.GPIO26, Part2.SDA
  N6: U1.GPIO14, A1.connector0
  GND: U1.GND, Part2.GND, A1.connector6, S1.leg0
  N7: U1.GPIO13, A1.connector3
  N8: U1.GPIO5, Part2.VIN
  N9: U1.GPIO18, A1.connector4
  N10: U1.GPIO21, A1.connector1
  N11: U1.GPIO22, A1.connector2
  N12: U1.GPIO23, A1.connector5
  N13: R1.Pin_1, U2.+
  N14: R2.Pin_0, U2.-

custom parts:
  ESP32S-HiLetgo: HiLetgo ESP-WROOM-32 ESP32 ESP-32S Development Board 2.4GHz Dual-Mode WiFi + Bluetooth Dual Cores Microcontroller The ESP32 integrated with Antenna switches, RF Balun, power amplifiers, low-noise amplifiers, filters, and management modules, and the entire solution occupies the least area of PCB. 2.4 GHz Wi-Fi plus Bluetooth dual-mode chip, with TSMC Ultra-low power consumption 40nm technology,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
