# Fritzing sketch nodemcu32s (saved by Fritzing 1.0.4)
breadboards: 1

parts:
  Part1 = node32s
  C1 = Electrolytic Capacitor [capacitance=0.1µF voltage=50V package="1010 [SMD, electrolytic]"]
  U1 = LIPO-2000mAh [package=lipo-2000]
  Part2 = BME280
  A1 = Waveshare e-Paper HAT with 7in display [package=THT]
  R1 = Resistor [tolerance=±5% resistance=680k package="1206 [SMD]"]
  R2 = Resistor [tolerance=±5% resistance=330k package="1206 [SMD]"]
  C3 = Ceramic Capacitor [capacitance="100 nF" voltage=35V package="1206 [SMD, multilayer]"]

nets:
  N1: Part1.IO34, R1.Pin_1, R2.Pin_0, C3.0
  N2: Part1.IO13, A1.pin_2
  N3: Part1.IO23, A1.pin_6
  N4: Part1.IO22, Part2.SCL
  N5: Part1.IO21, Part2.SDA
  N6: Part1.IO18, A1.pin_5
  N7: Part1.IO5, A1.pin_4
  N8: Part1.IO4, A1.pin_3
  N9: Part1.IO15, A1.pin_1
  N10: C1.-, U1.-, R2.Pin_1, C3.1
  N11: C1.+, U1.+, R1.Pin_0
  N12: Part2.VIN, A1.pin_8
  N13: Part2.GND, A1.pin_7

custom parts:
  Waveshare e-Paper HAT with 7in display: .This is a universal driver board for e-Paper raw panels, can be used to drive various SPI interface e-Paper from Waveshare. This version includes a 7in display panel in breadboard.
