# Fritzing sketch seedstudio xiao esp32-c6 (saved by Fritzing 1.0.4)
breadboards: 1

parts:
  C1 = Electrolytic Capacitor [capacitance=0.1mF voltage=35V package="1010 [SMD, electrolytic]"]
  C2 = Ceramic Capacitor [capacitance=0.1µF voltage=35V package="0805 [SMD, multilayer]"]
  U1 = LIPO-2000mAh [package=lipo-2000]
  R1 = Resistor [tolerance=±5% resistance=330k package="1206 [SMD]"]
  R2 = Resistor [tolerance=±5% resistance=150k package="1206 [SMD]"]
  S1 = Pushbutton [package="[SMD]"]
  Part1 = BME280
  A2 = Waveshare e-Paper HAT with 7in display [package=THT]
  R3 = Resistor [tolerance=±5% resistance=10k package="1206 [SMD]"]
  U2 = XIAO ESP32C6 [part_number=" XIAO ESP32C6"]

nets:
  N1: C1.-, C2.1, U1.-, R2.Pin_1
  N2: C1.+, U1.+, R1.Pin_0
  N3: C2.0, R1.Pin_1, R2.Pin_0, U2.D0
  N4: S1.Pin_1, S1.Pin_2, R3.Pin_1, U2.D2
  VIN: S1.Pin_3, S1.Pin_4, Part1.VIN, A2.pin_8, U2.3V3
  GND: Part1.GND, A2.pin_7, R3.Pin_0, U2.GND
  N5: Part1.SCL, U2.D5
  N6: Part1.SDA, U2.D4
  N7: A2.pin_1, U2.D9
  N8: A2.pin_2, U2.D7
  N9: A2.pin_3, U2.D3
  N10: A2.pin_4, U2.D6
  N11: A2.pin_5, U2.D8
  N12: A2.pin_6, U2.D10

custom parts:
  Waveshare e-Paper HAT with 7in display: .This is a universal driver board for e-Paper raw panels, can be used to drive various SPI interface e-Paper from Waveshare. This version includes a 7in display panel in breadboard.
  XIAO ESP32C6: XIAO ESP32C6 is a cost-effective MCU based on Espressif’s ESP32-C6. This compact MCU excels in Matter-compliant smart home applications with its support for various wireless connectivity (2.4GHz Wi-Fi 6, BLE 5.0, Zigbee, and Thread). Designed with the thumb-size footprint and a single-sided mount of the XIAO Series, it's perfect for space-limited projects. Encrypted on the chip, the XIAO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
